// Logisim project (4 MUX).circ as structural Verilog: 1 circuit, main circuit main
module main (
  input  [1:0] in_1,
  input  [3:0] INPUT_FOR_B,
  input  [3:0] INPUT_FOR_D,
  input  [3:0] INPUT_FOR_A,
  input  [3:0] INPUT_FOR_C,
  input  CLR,
  output [3:0] out_7,
  output [3:0] out_8,
  output [3:0] out_9,
  output [3:0] out_10,
  output [3:0] out_11
);

  wire clock_1_out;

  Clock clock_1 (.out(clock_1_out));
  Multiplexer #(.select(2), .enable("false")) multiplexer_1 (
    .in0(out_9[3]), .in1(out_8[3]), .in2(out_11[3]), .in3(out_10[3]), .out(out_7[3]), .sel(in_1));
  Register #(.width(4)) REGISTER_C (.D(INPUT_FOR_D), .en(1'b1), .Q(out_10), .clk(clock_1_out), .clr(CLR));
  Multiplexer #(.select(2), .enable("false")) multiplexer_2 (
    .in0(out_9[2]), .in1(out_8[2]), .in2(out_11[2]), .in3(out_10[2]), .out(out_7[2]), .sel(in_1));
  Register #(.width(4)) REGISTER_B (.D(INPUT_FOR_C), .en(1'b1), .Q(out_11), .clk(clock_1_out), .clr(CLR));
  Multiplexer #(.select(2), .enable("false")) multiplexer_3 (
    .in0(out_9[1]), .in1(out_8[1]), .in2(out_11[1]), .in3(out_10[1]), .out(out_7[1]), .sel(in_1));
  Register #(.width(4)) REGISTER_A (.D(INPUT_FOR_B), .en(1'b1), .Q(out_8), .clk(clock_1_out), .clr(CLR));
  Multiplexer #(.select(2), .enable("false")) multiplexer_4 (
    .in0(out_9[0]), .in1(out_8[0]), .in2(out_11[0]), .in3(out_10[0]), .out(out_7[0]), .sel(in_1));
  Register #(.width(4)) REGISTER_A_2 (.D(INPUT_FOR_A), .en(1'b1), .Q(out_9), .clk(clock_1_out), .clr(CLR));

  // Notes on the sheet:
  //   SELECT 00:A
  //   SELECT 01:B
  //   SELECT 10:C
  //   SELECT 11:D
  //   23CS060
endmodule
