// Logisim project (4D).circ as structural Verilog: 1 circuit, main circuit main
module main (
  input  [1:0] in_1,
  input  [3:0] in_2,
  input  [3:0] in_3,
  input  [3:0] in_4,
  input  [3:0] in_5,
  input  in_6,
  output [3:0] out_7,
  output [3:0] out_8,
  output [3:0] out_9,
  output [3:0] out_10,
  output [3:0] out_11
);

  wire clock_1_out, decoder_1_out0, decoder_1_out1, decoder_1_out2, decoder_1_out3;

  Clock clock_1 (.out(clock_1_out));
  Decoder #(.select(2), .enable("false")) decoder_1 (
    .out0(decoder_1_out0), .out1(decoder_1_out1), .out2(decoder_1_out2), .out3(decoder_1_out3), .sel(in_1));
  assign out_7[3] = decoder_1_out0 ? out_9[3] : 1'bz;  // Controlled_Buffer controlled_buffer_1
  assign out_7[3] = decoder_1_out1 ? out_8[3] : 1'bz;  // Controlled_Buffer controlled_buffer_2
  assign out_7[3] = decoder_1_out2 ? out_10[3] : 1'bz;  // Controlled_Buffer controlled_buffer_3
  assign out_7[3] = decoder_1_out3 ? out_11[3] : 1'bz;  // Controlled_Buffer controlled_buffer_4
  Register #(.width(4)) Rigester_D (.D(in_2), .en(1'b1), .Q(out_11), .clk(clock_1_out), .clr(in_6));
  assign out_7[2] = decoder_1_out0 ? out_9[2] : 1'bz;  // Controlled_Buffer controlled_buffer_5
  assign out_7[2] = decoder_1_out1 ? out_8[2] : 1'bz;  // Controlled_Buffer controlled_buffer_6
  assign out_7[2] = decoder_1_out2 ? out_10[2] : 1'bz;  // Controlled_Buffer controlled_buffer_7
  assign out_7[2] = decoder_1_out3 ? out_11[2] : 1'bz;  // Controlled_Buffer controlled_buffer_8
  assign out_7[1] = decoder_1_out0 ? out_9[1] : 1'bz;  // Controlled_Buffer controlled_buffer_9
  assign out_7[1] = decoder_1_out1 ? out_8[1] : 1'bz;  // Controlled_Buffer controlled_buffer_10
  assign out_7[1] = decoder_1_out2 ? out_10[1] : 1'bz;  // Controlled_Buffer controlled_buffer_11
  assign out_7[1] = decoder_1_out3 ? out_11[1] : 1'bz;  // Controlled_Buffer controlled_buffer_12
  Register #(.width(4)) Rigester_C (.D(in_3), .en(1'b1), .Q(out_10), .clk(clock_1_out), .clr(in_6));
  assign out_7[0] = decoder_1_out0 ? out_9[0] : 1'bz;  // Controlled_Buffer controlled_buffer_13
  assign out_7[0] = decoder_1_out1 ? out_8[0] : 1'bz;  // Controlled_Buffer controlled_buffer_14
  assign out_7[0] = decoder_1_out2 ? out_10[0] : 1'bz;  // Controlled_Buffer controlled_buffer_15
  assign out_7[0] = decoder_1_out3 ? out_11[0] : 1'bz;  // Controlled_Buffer controlled_buffer_16
  Register #(.width(4)) Rigester_B (.D(in_4), .en(1'b1), .Q(out_8), .clk(clock_1_out), .clr(in_6));
  Register #(.width(4)) Rigester_A (.D(in_5), .en(1'b1), .Q(out_9), .clk(clock_1_out), .clr(in_6));

  // Notes on the sheet:
  //   23CS060
endmodule
