// Logisim project USING DECODER.circ as structural Verilog: 1 circuit, main circuit main
module main (
  input  [1:0] SELECT_LINE,
  input  [2:0] INPUT_FOR_A,
  input  [2:0] INPUT_FOR_C,
  input  [2:0] INPUT_FOR_B,
  input  CLR,
  output [2:0] out_6,
  output [2:0] out_7,
  output [2:0] out_8,
  output [2:0] out_9
);

  wire clock_1_out, decoder_1_out0, decoder_1_out1, decoder_1_out2;

  Clock clock_1 (.out(clock_1_out));
  Decoder #(.select(2), .enable("false")) decoder_1 (
    .out0(decoder_1_out0), .out1(decoder_1_out1), .out2(decoder_1_out2), .sel(SELECT_LINE));  // open: out3
  Register #(.width(3)) REGISTER_C (.D(INPUT_FOR_C), .en(1'b1), .Q(out_8), .clk(clock_1_out), .clr(CLR));
  assign out_6[2] = decoder_1_out0 ? out_7[2] : 1'bz;  // Controlled_Buffer controlled_buffer_1
  assign out_6[2] = decoder_1_out1 ? out_9[2] : 1'bz;  // Controlled_Buffer controlled_buffer_2
  assign out_6[2] = decoder_1_out2 ? out_8[2] : 1'bz;  // Controlled_Buffer controlled_buffer_3
  assign out_6[0] = decoder_1_out0 ? out_7[0] : 1'bz;  // Controlled_Buffer controlled_buffer_4
  assign out_6[1] = decoder_1_out0 ? out_7[1] : 1'bz;  // Controlled_Buffer controlled_buffer_5
  assign out_6[1] = decoder_1_out1 ? out_9[1] : 1'bz;  // Controlled_Buffer controlled_buffer_6
  assign out_6[0] = decoder_1_out1 ? out_9[0] : 1'bz;  // Controlled_Buffer controlled_buffer_7
  assign out_6[1] = decoder_1_out2 ? out_8[1] : 1'bz;  // Controlled_Buffer controlled_buffer_8
  assign out_6[0] = decoder_1_out2 ? out_8[0] : 1'bz;  // Controlled_Buffer controlled_buffer_9
  Register #(.width(3)) REGISTER_B (.D(INPUT_FOR_B), .en(1'b1), .Q(out_9), .clk(clock_1_out), .clr(CLR));
  Register #(.width(3)) REGISTER_A (.D(INPUT_FOR_A), .en(1'b1), .Q(out_7), .clk(clock_1_out), .clr(CLR));

  // Notes on the sheet:
  //   SELECT 00:A
  //   SELECT 01:B
  //   SELECT 10:C
  //   M=(60%5)=3
  //   N=(60%3)=3
  //   A2
  //   B1
  //   B2
  //   C1
  //   C2
  //   23CS060
  //   A0
  //   A1
  //   B0
  //   C0
endmodule
