// Logisim project USING MUX.circ as structural Verilog: 1 circuit, main circuit main
module main (
  input  [1:0] SELECT,
  input  [2:0] INPUT_FOR_A,
  input  [2:0] INPUT_FOR_C,
  input  [2:0] INPUT_FOR_B,
  input  CLR,
  output [2:0] out_6,
  output [2:0] out_7,
  output [2:0] out_8,
  output [2:0] out_9
);

  wire clock_1_out;

  Clock clock_1 (.out(clock_1_out));
  Multiplexer #(.select(2), .enable("false")) multiplexer_1 (
    .in0(out_7[2]), .in1(out_9[2]), .in2(out_8[2]), .out(out_6[2]), .sel(SELECT));  // open: in3
  Register #(.width(3)) REGISTER_C (.D(INPUT_FOR_C), .en(1'b1), .Q(out_8), .clk(clock_1_out), .clr(CLR));
  Multiplexer #(.select(2), .enable("false")) multiplexer_2 (
    .in0(out_7[1]), .in1(out_9[1]), .in2(out_8[1]), .out(out_6[1]), .sel(SELECT));  // open: in3
  Register #(.width(3)) REGISTER_B (.D(INPUT_FOR_B), .en(1'b1), .Q(out_9), .clk(clock_1_out), .clr(CLR));
  Multiplexer #(.select(2), .enable("false")) multiplexer_3 (
    .in0(out_7[0]), .in1(out_9[0]), .in2(out_8[0]), .out(out_6[0]), .sel(SELECT));  // open: in3
  Register #(.width(3)) REGISTER_A (.D(INPUT_FOR_A), .en(1'b1), .Q(out_7), .clk(clock_1_out), .clr(CLR));

  // Notes on the sheet:
  //   SELECT 00:A
  //   SELECT 01:B
  //   SELECT 10:C
  //   M=(60%5)=3
  //   N=(60%3)=3
  //   BIT-3
  //   23CS060
  //   BIT-1
  //   BIT-0
endmodule
