// Logisim project CIRCUIT-1.circ as structural Verilog
module _1_BIT_ARITHMATIC (
  input  CIN,
  input  A,
  input  B,
  input  [1:0] S1S0,
  output S,
  output COUT
);

  wire multiplexer_1_out, not_1_out;

  not not_1 (not_1_out, B);
  Multiplexer #(.select(2), .enable("false")) multiplexer_1 (
    .in0(B), .in1(not_1_out), .in2(1'b0), .in3(1'b1), .out(multiplexer_1_out), .sel(S1S0));
  Adder #(.width(1)) adder_1 (.a(A), .b(multiplexer_1_out), .out(S), .cin(CIN), .cout(COUT));
endmodule

module _2_BIT_ARITHMATIC (
  input  CIN,
  input  A0,
  input  B0,
  input  A1,
  input  B1,
  input  [1:0] S1S0,
  output S0,
  output S1,
  output COUT
);

  wire adder_1_cout, multiplexer_1_out, multiplexer_2_out, not_1_out, not_2_out;

  not not_1 (not_1_out, B0);
  Multiplexer #(.select(2), .enable("false")) multiplexer_1 (
    .in0(B0), .in1(not_1_out), .in2(1'b0), .in3(1'b1), .out(multiplexer_1_out), .sel(S1S0));
  not not_2 (not_2_out, B1);
  Multiplexer #(.select(2), .enable("false")) multiplexer_2 (
    .in0(B1), .in1(not_2_out), .in2(1'b0), .in3(1'b1), .out(multiplexer_2_out), .sel(S1S0));
  Adder #(.width(1)) adder_1 (.a(A0), .b(multiplexer_1_out), .out(S0), .cin(CIN), .cout(adder_1_cout));
  Adder #(.width(1)) adder_2 (.a(A1), .b(multiplexer_2_out), .out(S1), .cin(adder_1_cout), .cout(COUT));
endmodule

module _4_BIT_ARITHMATIC (
  input  CIN,
  input  [3:0] A3A2A1A0,
  input  [3:0] B3B2B1B0,
  input  [1:0] S1S0,
  output [3:0] out_5,
  output COUT
);

  wire adder_1_cout, adder_2_cout, adder_3_cout, multiplexer_1_out, multiplexer_2_out, multiplexer_3_out,
       multiplexer_4_out, not_1_out, not_2_out, not_3_out, not_4_out;

  not not_1 (not_1_out, B3B2B1B0[0]);
  not not_2 (not_2_out, B3B2B1B0[1]);
  Multiplexer #(.select(2), .enable("false")) multiplexer_1 (
    .in0(B3B2B1B0[0]), .in1(not_1_out), .in2(1'b0), .in3(1'b1), .out(multiplexer_1_out), .sel(S1S0));
  Multiplexer #(.select(2), .enable("false")) multiplexer_2 (
    .in0(B3B2B1B0[1]), .in1(not_2_out), .in2(1'b0), .in3(1'b1), .out(multiplexer_2_out), .sel(S1S0));
  not not_3 (not_3_out, B3B2B1B0[2]);
  Multiplexer #(.select(2), .enable("false")) multiplexer_3 (
    .in0(B3B2B1B0[2]), .in1(not_3_out), .in2(1'b0), .in3(1'b1), .out(multiplexer_3_out), .sel(S1S0));
  not not_4 (not_4_out, B3B2B1B0[3]);
  Multiplexer #(.select(2), .enable("false")) multiplexer_4 (
    .in0(B3B2B1B0[3]), .in1(not_4_out), .in2(1'b0), .in3(1'b1), .out(multiplexer_4_out), .sel(S1S0));
  Adder #(.width(1)) adder_1 (.a(A3A2A1A0[0]), .b(multiplexer_1_out), .out(out_5[0]), .cin(CIN), .cout(adder_1_cout));
  Adder #(.width(1)) adder_2 (
    .a(A3A2A1A0[1]), .b(multiplexer_2_out), .out(out_5[1]), .cin(adder_1_cout), .cout(adder_2_cout));
  Adder #(.width(1)) adder_3 (
    .a(A3A2A1A0[2]), .b(multiplexer_3_out), .out(out_5[2]), .cin(adder_2_cout), .cout(adder_3_cout));
  Adder #(.width(1)) adder_4 (.a(A3A2A1A0[3]), .b(multiplexer_4_out), .out(out_5[3]), .cin(adder_3_cout), .cout(COUT));
endmodule

module _8_BIT_ARITHMATIC (
  input  CIN,
  input  [7:0] A7A6A5A3A2A1A0,
  input  [7:0] B7B6B5B3B2B1B0,
  input  [1:0] S1S0,
  output [7:0] out_5,
  output COUT
);

  wire adder_1_cout, adder_2_cout, adder_3_cout, adder_4_cout, adder_5_cout, adder_6_cout, adder_7_cout,
       multiplexer_1_out, multiplexer_2_out, multiplexer_3_out, multiplexer_4_out, multiplexer_5_out,
       multiplexer_6_out, multiplexer_7_out, multiplexer_8_out, not_1_out, not_2_out, not_3_out, not_4_out,
       not_5_out, not_6_out, not_7_out, not_8_out, not_9_out, not_10_out, not_11_out, not_12_out, not_13_out,
       not_14_out, not_15_out, not_16_out, xor_1_out, xor_2_out, xor_3_out, xor_4_out, xor_5_out, xor_6_out,
       xor_7_out, xor_8_out;

  xor xor_1 (xor_1_out, B7B6B5B3B2B1B0[0], B7B6B5B3B2B1B0[0]);
  not not_1 (not_1_out, xor_1_out);
  xor xor_2 (xor_2_out, B7B6B5B3B2B1B0[1], B7B6B5B3B2B1B0[1]);
  not not_2 (not_2_out, xor_2_out);
  xor xor_3 (xor_3_out, B7B6B5B3B2B1B0[2], B7B6B5B3B2B1B0[2]);
  not not_3 (not_3_out, xor_3_out);
  xor xor_4 (xor_4_out, B7B6B5B3B2B1B0[3], B7B6B5B3B2B1B0[3]);
  not not_4 (not_4_out, xor_4_out);
  xor xor_5 (xor_5_out, B7B6B5B3B2B1B0[4], B7B6B5B3B2B1B0[4]);
  not not_5 (not_5_out, xor_5_out);
  xor xor_6 (xor_6_out, B7B6B5B3B2B1B0[5], B7B6B5B3B2B1B0[5]);
  not not_6 (not_6_out, xor_6_out);
  xor xor_7 (xor_7_out, B7B6B5B3B2B1B0[6], B7B6B5B3B2B1B0[6]);
  not not_7 (not_7_out, xor_7_out);
  xor xor_8 (xor_8_out, B7B6B5B3B2B1B0[7], B7B6B5B3B2B1B0[7]);
  not not_8 (not_8_out, xor_8_out);
  not not_9 (not_9_out, B7B6B5B3B2B1B0[0]);
  Multiplexer #(.select(2), .enable("false")) multiplexer_1 (
    .in0(B7B6B5B3B2B1B0[0]), .in1(not_9_out), .in2(xor_1_out), .in3(not_1_out), .out(multiplexer_1_out),
    .sel(S1S0));
  not not_10 (not_10_out, B7B6B5B3B2B1B0[1]);
  Multiplexer #(.select(2), .enable("false")) multiplexer_2 (
    .in0(B7B6B5B3B2B1B0[1]), .in1(not_10_out), .in2(xor_2_out), .in3(not_2_out), .out(multiplexer_2_out),
    .sel(S1S0));
  not not_11 (not_11_out, B7B6B5B3B2B1B0[2]);
  Multiplexer #(.select(2), .enable("false")) multiplexer_3 (
    .in0(B7B6B5B3B2B1B0[2]), .in1(not_11_out), .in2(xor_3_out), .in3(not_3_out), .out(multiplexer_3_out),
    .sel(S1S0));
  not not_12 (not_12_out, B7B6B5B3B2B1B0[3]);
  Multiplexer #(.select(2), .enable("false")) multiplexer_4 (
    .in0(B7B6B5B3B2B1B0[3]), .in1(not_12_out), .in2(xor_4_out), .in3(not_4_out), .out(multiplexer_4_out),
    .sel(S1S0));
  not not_13 (not_13_out, B7B6B5B3B2B1B0[4]);
  Multiplexer #(.select(2), .enable("false")) multiplexer_5 (
    .in0(B7B6B5B3B2B1B0[4]), .in1(not_13_out), .in2(xor_5_out), .in3(not_5_out), .out(multiplexer_5_out),
    .sel(S1S0));
  not not_14 (not_14_out, B7B6B5B3B2B1B0[5]);
  Multiplexer #(.select(2), .enable("false")) multiplexer_6 (
    .in0(B7B6B5B3B2B1B0[5]), .in1(not_14_out), .in2(xor_6_out), .in3(not_6_out), .out(multiplexer_6_out),
    .sel(S1S0));
  not not_15 (not_15_out, B7B6B5B3B2B1B0[6]);
  Multiplexer #(.select(2), .enable("false")) multiplexer_7 (
    .in0(B7B6B5B3B2B1B0[6]), .in1(not_15_out), .in2(xor_7_out), .in3(not_7_out), .out(multiplexer_7_out),
    .sel(S1S0));
  not not_16 (not_16_out, B7B6B5B3B2B1B0[7]);
  Multiplexer #(.select(2), .enable("false")) multiplexer_8 (
    .in0(B7B6B5B3B2B1B0[7]), .in1(not_16_out), .in2(xor_8_out), .in3(not_8_out), .out(multiplexer_8_out),
    .sel(S1S0));
  Adder #(.width(1)) adder_1 (
    .a(A7A6A5A3A2A1A0[0]), .b(multiplexer_1_out), .out(out_5[0]), .cin(CIN), .cout(adder_1_cout));
  Adder #(.width(1)) adder_2 (
    .a(A7A6A5A3A2A1A0[1]), .b(multiplexer_2_out), .out(out_5[1]), .cin(adder_1_cout), .cout(adder_2_cout));
  Adder #(.width(1)) adder_3 (
    .a(A7A6A5A3A2A1A0[2]), .b(multiplexer_3_out), .out(out_5[2]), .cin(adder_2_cout), .cout(adder_3_cout));
  Adder #(.width(1)) adder_4 (
    .a(A7A6A5A3A2A1A0[3]), .b(multiplexer_4_out), .out(out_5[3]), .cin(adder_3_cout), .cout(adder_4_cout));
  Adder #(.width(1)) adder_5 (
    .a(A7A6A5A3A2A1A0[4]), .b(multiplexer_5_out), .out(out_5[4]), .cin(adder_4_cout), .cout(adder_5_cout));
  Adder #(.width(1)) adder_6 (
    .a(A7A6A5A3A2A1A0[5]), .b(multiplexer_6_out), .out(out_5[5]), .cin(adder_5_cout), .cout(adder_6_cout));
  Adder #(.width(1)) adder_7 (
    .a(A7A6A5A3A2A1A0[6]), .b(multiplexer_7_out), .out(out_5[6]), .cin(adder_6_cout), .cout(adder_7_cout));
  Adder #(.width(1)) adder_8 (
    .a(A7A6A5A3A2A1A0[7]), .b(multiplexer_8_out), .out(out_5[7]), .cin(adder_7_cout), .cout(COUT));
endmodule

module _1_BIT_LOGICAL_CIRCUIT (
  input  BO,
  input  A0,
  input  [1:0] S1S0,
  output E0
);

  wire and_1_out, not_1_out, or_1_out, xor_1_out;

  and and_1 (and_1_out, A0, BO);
  or or_1 (or_1_out, A0, BO);
  xor xor_1 (xor_1_out, A0, BO);
  not not_1 (not_1_out, A0);
  Multiplexer #(.select(2), .enable("false")) multiplexer_1 (
    .in0(and_1_out), .in1(or_1_out), .in2(xor_1_out), .in3(not_1_out), .out(E0), .sel(S1S0));
endmodule

module _2_BIT_LOGIC (
  input  [1:0] B1B0,
  input  [1:0] A1A0,
  input  [1:0] S1S0,
  output [1:0] E1E0
);

  wire and_1_out, and_2_out, not_1_out, not_2_out, or_1_out, or_2_out, xor_1_out, xor_2_out;

  and and_1 (and_1_out, A1A0[0], B1B0[0]);
  or or_1 (or_1_out, A1A0[0], B1B0[0]);
  xor xor_1 (xor_1_out, A1A0[0], B1B0[0]);
  not not_1 (not_1_out, A1A0[0]);
  and and_2 (and_2_out, A1A0[1], B1B0[1]);
  or or_2 (or_2_out, A1A0[1], B1B0[1]);
  xor xor_2 (xor_2_out, A1A0[1], B1B0[1]);
  not not_2 (not_2_out, A1A0[1]);
  Multiplexer #(.select(2), .enable("false")) multiplexer_1 (
    .in0(and_1_out), .in1(or_1_out), .in2(xor_1_out), .in3(not_1_out), .out(E1E0[0]), .sel(S1S0));
  Multiplexer #(.select(2), .enable("false")) multiplexer_2 (
    .in0(and_2_out), .in1(or_2_out), .in2(xor_2_out), .in3(not_2_out), .out(E1E0[1]), .sel(S1S0));
endmodule

module _4_BIT_LOGICAL (
  input  [3:0] B3B2B1B0,
  input  [3:0] A3A2A1A0,
  input  [1:0] S1S0,
  output [3:0] E3E2E1E0
);

  wire and_1_out, and_2_out, and_3_out, and_4_out, not_1_out, not_2_out, not_3_out, not_4_out, or_1_out,
       or_2_out, or_3_out, or_4_out, xor_1_out, xor_2_out, xor_3_out, xor_4_out;

  not not_1 (not_1_out, A3A2A1A0[2]);
  and and_1 (and_1_out, A3A2A1A0[3], B3B2B1B0[3]);
  or or_1 (or_1_out, A3A2A1A0[3], B3B2B1B0[3]);
  xor xor_1 (xor_1_out, A3A2A1A0[3], B3B2B1B0[3]);
  not not_2 (not_2_out, A3A2A1A0[3]);
  and and_2 (and_2_out, A3A2A1A0[0], B3B2B1B0[0]);
  or or_2 (or_2_out, A3A2A1A0[0], B3B2B1B0[0]);
  xor xor_2 (xor_2_out, A3A2A1A0[0], B3B2B1B0[0]);
  not not_3 (not_3_out, A3A2A1A0[0]);
  and and_3 (and_3_out, A3A2A1A0[1], B3B2B1B0[1]);
  or or_3 (or_3_out, A3A2A1A0[1], B3B2B1B0[1]);
  xor xor_3 (xor_3_out, A3A2A1A0[1], B3B2B1B0[1]);
  not not_4 (not_4_out, A3A2A1A0[1]);
  and and_4 (and_4_out, A3A2A1A0[2], B3B2B1B0[2]);
  or or_4 (or_4_out, A3A2A1A0[2], B3B2B1B0[2]);
  xor xor_4 (xor_4_out, A3A2A1A0[2], B3B2B1B0[2]);
  Multiplexer #(.select(2), .enable("false")) multiplexer_1 (
    .in0(and_4_out), .in1(or_4_out), .in2(xor_4_out), .in3(not_1_out), .out(E3E2E1E0[2]), .sel(S1S0));
  Multiplexer #(.select(2), .enable("false")) multiplexer_2 (
    .in0(and_1_out), .in1(or_1_out), .in2(xor_1_out), .in3(not_2_out), .out(E3E2E1E0[3]), .sel(S1S0));
  Multiplexer #(.select(2), .enable("false")) multiplexer_3 (
    .in0(and_2_out), .in1(or_2_out), .in2(xor_2_out), .in3(not_3_out), .out(E3E2E1E0[0]), .sel(S1S0));
  Multiplexer #(.select(2), .enable("false")) multiplexer_4 (
    .in0(and_3_out), .in1(or_3_out), .in2(xor_3_out), .in3(not_4_out), .out(E3E2E1E0[1]), .sel(S1S0));
endmodule

module _8_BIT_LOGICAL (
  input  [7:0] B6B5B4B3B2B1B0,
  input  [7:0] A7A6A5A4A3A2A1A0,
  input  [1:0] S1S0,
  output [7:0] E7E6E5E4E3E2E1E0
);

  wire and_1_out, and_2_out, and_3_out, and_4_out, and_5_out, and_6_out, and_7_out, and_8_out, not_1_out,
       not_2_out, not_3_out, not_4_out, not_5_out, not_6_out, not_7_out, not_8_out, or_1_out, or_2_out,
       or_3_out, or_4_out, or_5_out, or_6_out, or_7_out, or_8_out, xor_1_out, xor_2_out, xor_3_out,
       xor_4_out, xor_5_out, xor_6_out, xor_7_out, xor_8_out;

  not not_1 (not_1_out, A7A6A5A4A3A2A1A0[4]);
  and and_1 (and_1_out, A7A6A5A4A3A2A1A0[0], B6B5B4B3B2B1B0[0]);
  or or_1 (or_1_out, A7A6A5A4A3A2A1A0[0], B6B5B4B3B2B1B0[0]);
  xor xor_1 (xor_1_out, A7A6A5A4A3A2A1A0[0], B6B5B4B3B2B1B0[0]);
  not not_2 (not_2_out, A7A6A5A4A3A2A1A0[0]);
  and and_2 (and_2_out, A7A6A5A4A3A2A1A0[1], B6B5B4B3B2B1B0[1]);
  or or_2 (or_2_out, A7A6A5A4A3A2A1A0[1], B6B5B4B3B2B1B0[1]);
  xor xor_2 (xor_2_out, A7A6A5A4A3A2A1A0[1], B6B5B4B3B2B1B0[1]);
  not not_3 (not_3_out, A7A6A5A4A3A2A1A0[1]);
  and and_3 (and_3_out, A7A6A5A4A3A2A1A0[2], B6B5B4B3B2B1B0[2]);
  or or_3 (or_3_out, A7A6A5A4A3A2A1A0[2], B6B5B4B3B2B1B0[2]);
  xor xor_3 (xor_3_out, A7A6A5A4A3A2A1A0[2], B6B5B4B3B2B1B0[2]);
  not not_4 (not_4_out, A7A6A5A4A3A2A1A0[2]);
  and and_4 (and_4_out, A7A6A5A4A3A2A1A0[3], B6B5B4B3B2B1B0[3]);
  or or_4 (or_4_out, A7A6A5A4A3A2A1A0[3], B6B5B4B3B2B1B0[3]);
  xor xor_4 (xor_4_out, A7A6A5A4A3A2A1A0[3], B6B5B4B3B2B1B0[3]);
  not not_5 (not_5_out, A7A6A5A4A3A2A1A0[3]);
  and and_5 (and_5_out, A7A6A5A4A3A2A1A0[4], B6B5B4B3B2B1B0[4]);
  or or_5 (or_5_out, A7A6A5A4A3A2A1A0[4], B6B5B4B3B2B1B0[4]);
  xor xor_5 (xor_5_out, A7A6A5A4A3A2A1A0[4], B6B5B4B3B2B1B0[4]);
  and and_6 (and_6_out, A7A6A5A4A3A2A1A0[5], B6B5B4B3B2B1B0[5]);
  or or_6 (or_6_out, A7A6A5A4A3A2A1A0[5], B6B5B4B3B2B1B0[5]);
  xor xor_6 (xor_6_out, A7A6A5A4A3A2A1A0[5], B6B5B4B3B2B1B0[5]);
  not not_6 (not_6_out, A7A6A5A4A3A2A1A0[5]);
  and and_7 (and_7_out, A7A6A5A4A3A2A1A0[6], B6B5B4B3B2B1B0[6]);
  or or_7 (or_7_out, A7A6A5A4A3A2A1A0[6], B6B5B4B3B2B1B0[6]);
  xor xor_7 (xor_7_out, A7A6A5A4A3A2A1A0[6], B6B5B4B3B2B1B0[6]);
  not not_7 (not_7_out, A7A6A5A4A3A2A1A0[6]);
  and and_8 (and_8_out, A7A6A5A4A3A2A1A0[7], B6B5B4B3B2B1B0[7]);
  or or_8 (or_8_out, A7A6A5A4A3A2A1A0[7], B6B5B4B3B2B1B0[7]);
  xor xor_8 (xor_8_out, A7A6A5A4A3A2A1A0[7], B6B5B4B3B2B1B0[7]);
  not not_8 (not_8_out, A7A6A5A4A3A2A1A0[7]);
  Multiplexer #(.select(2), .enable("false")) multiplexer_1 (
    .in0(and_1_out), .in1(or_1_out), .in2(xor_1_out), .in3(not_2_out), .out(E7E6E5E4E3E2E1E0[0]), .sel(S1S0));
  Multiplexer #(.select(2), .enable("false")) multiplexer_2 (
    .in0(and_2_out), .in1(or_2_out), .in2(xor_2_out), .in3(not_3_out), .out(E7E6E5E4E3E2E1E0[1]), .sel(S1S0));
  Multiplexer #(.select(2), .enable("false")) multiplexer_3 (
    .in0(and_3_out), .in1(or_3_out), .in2(xor_3_out), .in3(not_4_out), .out(E7E6E5E4E3E2E1E0[2]), .sel(S1S0));
  Multiplexer #(.select(2), .enable("false")) multiplexer_4 (
    .in0(and_4_out), .in1(or_4_out), .in2(xor_4_out), .in3(not_5_out), .out(E7E6E5E4E3E2E1E0[3]), .sel(S1S0));
  Multiplexer #(.select(2), .enable("false")) multiplexer_5 (
    .in0(and_5_out), .in1(or_5_out), .in2(xor_5_out), .in3(not_1_out), .out(E7E6E5E4E3E2E1E0[4]), .sel(S1S0));
  Multiplexer #(.select(2), .enable("false")) multiplexer_6 (
    .in0(and_6_out), .in1(or_6_out), .in2(xor_6_out), .in3(not_6_out), .out(E7E6E5E4E3E2E1E0[5]), .sel(S1S0));
  Multiplexer #(.select(2), .enable("false")) multiplexer_7 (
    .in0(and_7_out), .in1(or_7_out), .in2(xor_7_out), .in3(not_7_out), .out(E7E6E5E4E3E2E1E0[6]), .sel(S1S0));
  Multiplexer #(.select(2), .enable("false")) multiplexer_8 (
    .in0(and_8_out), .in1(or_8_out), .in2(xor_8_out), .in3(not_8_out), .out(E7E6E5E4E3E2E1E0[7]), .sel(S1S0));
endmodule

module _1_BIT_LOGICAL_FUNCTION (
  input  A0,
  input  B0,
  input  [3:0] S3S2S1S0,
  output out_4
);

  wire and_1_out, and_2_out, and_3_out, nand_1_out, not_1_out, not_2_out, not_3_out, not_4_out, or_1_out,
       or_2_out, or_3_out, xor_1_out;

  not not_1 (not_1_out, A0);
  not not_2 (not_2_out, B0);
  and and_1 (and_1_out, A0, B0);
  and and_2 (and_2_out, A0, not_2_out);
  and and_3 (and_3_out, not_1_out, B0);
  xor xor_1 (xor_1_out, A0, B0);
  or or_1 (or_1_out, A0, B0);
  not not_3 (not_3_out, or_1_out);
  not not_4 (not_4_out, xor_1_out);
  or or_2 (or_2_out, A0, not_2_out);
  or or_3 (or_3_out, not_1_out, B0);
  nand nand_1 (nand_1_out, A0, B0);
  Multiplexer #(.select(4), .enable("false")) multiplexer_1 (
    .in0(1'b0), .in1(and_1_out), .in2(and_2_out), .in3(A0), .in4(and_3_out), .in5(B0), .in6(xor_1_out),
    .in7(or_1_out), .in8(not_3_out), .in9(not_4_out), .in10(not_2_out), .in11(or_2_out), .in12(not_1_out),
    .in13(or_3_out), .in14(nand_1_out), .in15(1'b1), .out(out_4), .sel(S3S2S1S0));
endmodule

module _2_BIT_LOGIC_FUNCTION (
  input  [1:0] B1B0,
  input  [1:0] A1A0,
  input  [3:0] S3S2S1S0,
  output [1:0] E1E0
);

  wire and_1_out, and_2_out, and_3_out, and_4_out, and_5_out, and_6_out, nand_1_out, nand_2_out, not_1_out,
       not_2_out, not_3_out, not_4_out, not_5_out, not_6_out, not_7_out, not_8_out, or_1_out, or_2_out,
       or_3_out, or_4_out, or_5_out, or_6_out, xor_1_out, xor_2_out;

  not not_1 (not_1_out, B1B0[0]);
  not not_2 (not_2_out, A1A0[0]);
  not not_3 (not_3_out, A1A0[1]);
  not not_4 (not_4_out, B1B0[1]);
  and and_1 (and_1_out, A1A0[0], B1B0[0]);
  and and_2 (and_2_out, A1A0[0], not_1_out);
  and and_3 (and_3_out, not_2_out, B1B0[0]);
  xor xor_1 (xor_1_out, A1A0[0], B1B0[0]);
  or or_1 (or_1_out, A1A0[0], B1B0[0]);
  not not_5 (not_5_out, or_1_out);
  not not_6 (not_6_out, xor_1_out);
  or or_2 (or_2_out, A1A0[0], not_1_out);
  or or_3 (or_3_out, not_2_out, B1B0[0]);
  nand nand_1 (nand_1_out, A1A0[0], B1B0[0]);
  and and_4 (and_4_out, A1A0[1], B1B0[1]);
  and and_5 (and_5_out, A1A0[1], not_4_out);
  and and_6 (and_6_out, not_3_out, B1B0[1]);
  xor xor_2 (xor_2_out, A1A0[1], B1B0[1]);
  or or_4 (or_4_out, A1A0[1], B1B0[1]);
  not not_7 (not_7_out, or_4_out);
  not not_8 (not_8_out, xor_2_out);
  or or_5 (or_5_out, A1A0[1], not_4_out);
  or or_6 (or_6_out, not_3_out, B1B0[1]);
  nand nand_2 (nand_2_out, A1A0[1], B1B0[1]);
  Multiplexer #(.select(4), .enable("false")) multiplexer_1 (
    .in0(1'b0), .in1(and_1_out), .in2(and_2_out), .in3(A1A0[0]), .in4(and_3_out), .in5(B1B0[0]),
    .in6(xor_1_out), .in7(or_1_out), .in8(not_5_out), .in9(not_6_out), .in10(not_1_out), .in11(or_2_out),
    .in12(not_2_out), .in13(or_3_out), .in14(nand_1_out), .in15(1'b1), .out(E1E0[0]), .sel(S3S2S1S0));
  Multiplexer #(.select(4), .enable("false")) multiplexer_2 (
    .in0(1'b0), .in1(and_4_out), .in2(and_5_out), .in3(A1A0[1]), .in4(and_6_out), .in5(B1B0[1]),
    .in6(xor_2_out), .in7(or_4_out), .in8(not_7_out), .in9(not_8_out), .in10(not_4_out), .in11(or_5_out),
    .in12(not_3_out), .in13(or_6_out), .in14(nand_2_out), .in15(1'b1), .out(E1E0[1]), .sel(S3S2S1S0));
endmodule
