// Logisim project EXP-5.circ as structural Verilog
module _1_BIT_ARITHMATIC (
  input  CIN,
  input  A,
  input  B,
  input  [1:0] S1S0,
  output S,
  output COUT
);

  wire multiplexer_1_out, not_1_out;

  not not_1 (not_1_out, B);
  Multiplexer #(.select(2), .enable("false")) multiplexer_1 (
    .in0(B), .in1(not_1_out), .in2(1'b0), .in3(1'b1), .out(multiplexer_1_out), .sel(S1S0));
  Adder #(.width(1)) adder_1 (.a(A), .b(multiplexer_1_out), .out(S), .cin(CIN), .cout(COUT));

  // Notes on the sheet:
  //   1 BIT ARITHMATIC
  //   23CS060
endmodule

module _1_BIT_LOGICAL_CIRCUIT (
  input  BO,
  input  A0,
  input  [1:0] S1S0,
  output E0
);

  wire and_1_out, not_1_out, or_1_out, xor_1_out;

  and and_1 (and_1_out, A0, BO);
  or or_1 (or_1_out, A0, BO);
  xor xor_1 (xor_1_out, A0, BO);
  not not_1 (not_1_out, A0);
  Multiplexer #(.select(2), .enable("false")) multiplexer_1 (
    .in0(and_1_out), .in1(or_1_out), .in2(xor_1_out), .in3(not_1_out), .out(E0), .sel(S1S0));

  // Notes on the sheet:
  //   23CS060
  //   1  BIT LOGICAL
endmodule

module _8_BIT_ALU (
  input  [3:0] SELECT,
  input  SHL,
  input  SHR,
  input  [7:0] A,
  input  CIN,
  input  [7:0] B,
  output COUT,
  output [7:0] O_P
);

  wire n1_bit_arithmatic_1_cout, n1_bit_arithmatic_1_s, n1_bit_arithmatic_2_cout, n1_bit_arithmatic_2_s,
       n1_bit_arithmatic_3_cout, n1_bit_arithmatic_3_s, n1_bit_arithmatic_4_cout, n1_bit_arithmatic_4_s,
       n1_bit_arithmatic_5_cout, n1_bit_arithmatic_5_s, n1_bit_arithmatic_6_cout, n1_bit_arithmatic_6_s,
       n1_bit_arithmatic_7_cout, n1_bit_arithmatic_7_s, n1_bit_arithmatic_8_s, n1_bit_logical_circuit_1_e0,
       n1_bit_logical_circuit_2_e0, n1_bit_logical_circuit_3_e0, n1_bit_logical_circuit_4_e0,
       n1_bit_logical_circuit_5_e0, n1_bit_logical_circuit_6_e0, n1_bit_logical_circuit_7_e0,
       n1_bit_logical_circuit_8_e0;

  _1_BIT_ARITHMATIC u_1_bit_arithmatic_1 (
    .A(A[0]), .B(B[0]), .S1S0(SELECT[1:0]), .CIN(CIN), .S(n1_bit_arithmatic_1_s),
    .COUT(n1_bit_arithmatic_1_cout));
  _1_BIT_LOGICAL_CIRCUIT u_1_bit_logical_circuit_1 (
    .S1S0(SELECT[1:0]), .BO(B[0]), .A0(A[0]), .E0(n1_bit_logical_circuit_1_e0));
  _1_BIT_ARITHMATIC u_1_bit_arithmatic_2 (
    .A(A[1]), .B(B[1]), .S1S0(SELECT[1:0]), .CIN(n1_bit_arithmatic_1_cout), .S(n1_bit_arithmatic_2_s),
    .COUT(n1_bit_arithmatic_2_cout));
  _1_BIT_LOGICAL_CIRCUIT u_1_bit_logical_circuit_2 (
    .S1S0(SELECT[1:0]), .BO(B[1]), .A0(A[1]), .E0(n1_bit_logical_circuit_2_e0));
  _1_BIT_ARITHMATIC u_1_bit_arithmatic_3 (
    .A(A[2]), .B(B[2]), .S1S0(SELECT[1:0]), .CIN(n1_bit_arithmatic_2_cout), .S(n1_bit_arithmatic_3_s),
    .COUT(n1_bit_arithmatic_3_cout));
  _1_BIT_LOGICAL_CIRCUIT u_1_bit_logical_circuit_3 (
    .S1S0(SELECT[1:0]), .BO(B[2]), .A0(A[2]), .E0(n1_bit_logical_circuit_3_e0));
  _1_BIT_ARITHMATIC u_1_bit_arithmatic_4 (
    .A(A[3]), .B(B[3]), .S1S0(SELECT[1:0]), .CIN(n1_bit_arithmatic_3_cout), .S(n1_bit_arithmatic_4_s),
    .COUT(n1_bit_arithmatic_4_cout));
  _1_BIT_LOGICAL_CIRCUIT u_1_bit_logical_circuit_4 (
    .S1S0(SELECT[1:0]), .BO(B[3]), .A0(A[3]), .E0(n1_bit_logical_circuit_4_e0));
  _1_BIT_ARITHMATIC u_1_bit_arithmatic_5 (
    .A(A[4]), .B(B[4]), .S1S0(SELECT[1:0]), .CIN(n1_bit_arithmatic_4_cout), .S(n1_bit_arithmatic_5_s),
    .COUT(n1_bit_arithmatic_5_cout));
  _1_BIT_LOGICAL_CIRCUIT u_1_bit_logical_circuit_5 (
    .S1S0(SELECT[1:0]), .BO(B[4]), .A0(A[4]), .E0(n1_bit_logical_circuit_5_e0));
  _1_BIT_ARITHMATIC u_1_bit_arithmatic_6 (
    .A(A[5]), .B(B[5]), .S1S0(SELECT[1:0]), .CIN(n1_bit_arithmatic_5_cout), .S(n1_bit_arithmatic_6_s),
    .COUT(n1_bit_arithmatic_6_cout));
  _1_BIT_LOGICAL_CIRCUIT u_1_bit_logical_circuit_6 (
    .S1S0(SELECT[1:0]), .BO(B[5]), .A0(A[5]), .E0(n1_bit_logical_circuit_6_e0));
  _1_BIT_ARITHMATIC u_1_bit_arithmatic_7 (
    .A(A[6]), .B(B[6]), .S1S0(SELECT[1:0]), .CIN(n1_bit_arithmatic_6_cout), .S(n1_bit_arithmatic_7_s),
    .COUT(n1_bit_arithmatic_7_cout));
  _1_BIT_LOGICAL_CIRCUIT u_1_bit_logical_circuit_7 (
    .S1S0(SELECT[1:0]), .BO(B[6]), .A0(A[6]), .E0(n1_bit_logical_circuit_7_e0));
  _1_BIT_ARITHMATIC u_1_bit_arithmatic_8 (
    .A(A[7]), .B(B[7]), .S1S0(SELECT[1:0]), .CIN(n1_bit_arithmatic_7_cout), .S(n1_bit_arithmatic_8_s),
    .COUT(COUT));
  _1_BIT_LOGICAL_CIRCUIT u_1_bit_logical_circuit_8 (
    .S1S0(SELECT[1:0]), .BO(B[7]), .A0(A[7]), .E0(n1_bit_logical_circuit_8_e0));
  Multiplexer #(.select(2), .enable("false")) multiplexer_1 (
    .in0(n1_bit_arithmatic_1_s), .in1(n1_bit_logical_circuit_1_e0), .in2(A[1]), .in3(SHL), .out(O_P[0]),
    .sel(SELECT[3:2]));
  Multiplexer #(.select(2), .enable("false")) multiplexer_2 (
    .in0(n1_bit_arithmatic_2_s), .in1(n1_bit_logical_circuit_2_e0), .in2(A[2]), .in3(A[0]), .out(O_P[1]),
    .sel(SELECT[3:2]));
  Multiplexer #(.select(2), .enable("false")) multiplexer_3 (
    .in0(n1_bit_arithmatic_3_s), .in1(n1_bit_logical_circuit_3_e0), .in2(A[3]), .in3(A[1]), .out(O_P[2]),
    .sel(SELECT[3:2]));
  Multiplexer #(.select(2), .enable("false")) multiplexer_4 (
    .in0(n1_bit_arithmatic_4_s), .in1(n1_bit_logical_circuit_4_e0), .in2(A[4]), .in3(A[2]), .out(O_P[3]),
    .sel(SELECT[3:2]));
  Multiplexer #(.select(2), .enable("false")) multiplexer_5 (
    .in0(n1_bit_arithmatic_5_s), .in1(n1_bit_logical_circuit_5_e0), .in2(A[5]), .in3(A[3]), .out(O_P[4]),
    .sel(SELECT[3:2]));
  Multiplexer #(.select(2), .enable("false")) multiplexer_6 (
    .in0(n1_bit_arithmatic_6_s), .in1(n1_bit_logical_circuit_6_e0), .in2(A[6]), .in3(A[4]), .out(O_P[5]),
    .sel(SELECT[3:2]));
  Multiplexer #(.select(2), .enable("false")) multiplexer_7 (
    .in0(n1_bit_arithmatic_7_s), .in1(n1_bit_logical_circuit_7_e0), .in2(A[7]), .in3(A[5]), .out(O_P[6]),
    .sel(SELECT[3:2]));
  Multiplexer #(.select(2), .enable("false")) multiplexer_8 (
    .in0(n1_bit_arithmatic_8_s), .in1(n1_bit_logical_circuit_8_e0), .in2(SHR), .in3(A[6]), .out(O_P[7]),
    .sel(SELECT[3:2]));

  // Notes on the sheet:
  //   B7B6B5B4B2B1B0
  //   8 BIT ALU
  //   A7A6A5A4A3A2A1A0
  //   S3S2S1S0
  //   23CS060
endmodule

module CIRCUIT_1 (
  input  [3:0] S3S2S1S0,
  input  CIN,
  input  SHL,
  input  [15:0] A,
  input  [15:0] B,
  input  SHR,
  output [15:0] OUTPUT,
  output COUT
);

  wire n8_bit_alu_1_cout;

  _8_BIT_ALU u_8_bit_alu_1 (
    .SELECT(S3S2S1S0), .A(A[7:0]), .CIN(CIN), .B(B[7:0]), .SHL(SHL), .SHR(A[8]), .O_P(OUTPUT[7:0]),
    .COUT(n8_bit_alu_1_cout));
  _8_BIT_ALU u_8_bit_alu_2 (
    .SELECT(S3S2S1S0), .A(A[15:8]), .CIN(n8_bit_alu_1_cout), .B(B[15:8]), .SHL(A[7]), .SHR(SHR),
    .O_P(OUTPUT[15:8]), .COUT(COUT));

  // Notes on the sheet:
  //   23CS060
  //   23CS060
endmodule

module COMMON__BUS (
  input  [11:0] in_1,
  input  SELECT_ADD,
  input  CLR,
  input  W,
  input  CS,
  input  LOAD,
  input  LD_AR,
  input  [15:0] MUX_B,
  input  INC_AR,
  input  SELECT_DATA,
  input  CL_AR,
  input  LD_PC,
  input  INC_PC,
  input  CL_PC,
  input  LD_DR,
  input  INC_DR,
  input  CL_DR,
  input  CL_AR_2,
  input  [3:0] S3S2S1S0,
  input  SHL,
  input  CIN,
  input  LD_AC,
  input  [2:0] S2S1S0,
  input  CL_AC,
  input  [1:0] SEL_1,
  input  SHR,
  input  INC_AC,
  input  LD_IR,
  input  [1:0] SEL_2,
  input  CL_IR,
  input  [7:0] INPUT_R,
  input  LD_TR,
  input  CL_TR,
  input  CL_O_PR,
  input  LD_O_PR,
  output [15:0] CB_OUTPUT,
  output COUT
);

  wire CLK_2_out, CLK_out, clock_1_out;
  wire [11:0] AR_q, multiplexer_1_out, PC_q;
  wire [15:0] AC_q, circuit_1_1_output, DR_q, IR_q, multiplexer_2_out, multiplexer_3_out, multiplexer_4_out,
       multiplexer_5_out, ram_1_data, TR_q;

  Multiplexer #(.width(12), .enable("false")) multiplexer_1 (
    .in0(AR_q), .in1(in_1), .out(multiplexer_1_out), .sel(SELECT_ADD));
  Multiplexer #(.width(16), .enable("false")) multiplexer_2 (
    .in0(CB_OUTPUT), .in1(MUX_B), .out(multiplexer_2_out), .sel(SELECT_DATA));
  Multiplexer #(.select(2), .width(16), .enable("false")) multiplexer_3 (
    .in0(AC_q), .in1(DR_q), .in2({{8{1'b0}}, INPUT_R}), .out(multiplexer_3_out), .sel(SEL_1));  // open: in3
  Multiplexer #(.select(2), .width(16), .enable("false")) multiplexer_4 (
    .in0(AC_q), .in1(DR_q), .in2({{8{1'b0}}, INPUT_R}), .out(multiplexer_4_out), .sel(SEL_2));  // open: in3
  Clock clock_1 (.out(clock_1_out));
  CIRCUIT_1 circuit_1_1 (
    .S3S2S1S0(S3S2S1S0), .A(multiplexer_3_out), .B(multiplexer_4_out), .CIN(CIN), .SHL(SHL), .SHR(SHR),
    .OUTPUT(circuit_1_1_output), .COUT(COUT));
  RAM #(.addrWidth(12), .dataWidth(16), .bus("separate")) ram_1 (
    .addr(multiplexer_1_out), .din(multiplexer_2_out), .data(ram_1_data), .str(W), .sel(CS),
    .clk(clock_1_out), .ld(LOAD), .clr(CLR));
  Register #(.width(16)) IR (.D(CB_OUTPUT), .en(LD_IR), .Q(IR_q), .clk(CLK_out), .clr(CL_IR));
  Register #(.width(16)) TR (.D(CB_OUTPUT), .en(LD_TR), .Q(TR_q), .clk(CLK_out), .clr(CL_TR));
  Clock CLK (.out(CLK_out));
  Counter #(.width(12), .max('hfff)) AR (
    .load(LD_AR), .D(CB_OUTPUT[11:0]), .count(INC_AR), .Q(AR_q), .clk(CLK_out), .clr(CL_AR));  // open: carry
  Counter #(.width(12), .max('hfff)) PC (
    .load(LD_PC), .D(CB_OUTPUT[11:0]), .count(INC_PC), .Q(PC_q), .clk(CLK_out), .clr(CL_PC));  // open: carry
  Counter #(.width(16), .max('hffff)) DR (
    .load(LD_DR), .D(CB_OUTPUT), .count(INC_DR), .Q(DR_q), .clk(CLK_out), .clr(CL_DR));  // open: carry
  Counter #(.width(16), .max('hffff)) AC (
    .load(LD_AC), .D(circuit_1_1_output), .count(INC_AC), .Q(AC_q), .clk(CLK_out), .clr(CL_AC));  // open: carry
  Register O_PR (.D(CB_OUTPUT[7:0]), .en(LD_O_PR), .clk(CLK_out), .clr(CL_O_PR));  // open: Q
  Multiplexer #(.select(3), .width(16), .enable("false")) multiplexer_5 (
    .in1({4'b0000, AR_q}), .in2({4'b0000, PC_q}), .in3(DR_q), .in4(AC_q), .in5(IR_q), .in6(TR_q),
    .in7(ram_1_data), .out(multiplexer_5_out), .sel(S2S1S0));  // open: in0
  Clock CLK_2 (.out(CLK_2_out));
  Counter #(.width(16), .max('hffff)) counter_1 (
    .load(1'b1), .D(multiplexer_5_out), .count(1'b0), .Q(CB_OUTPUT), .clk(CLK_2_out), .clr(CL_AR_2));  // open: carry

  // Notes on the sheet:
  //   MUX A
  //   23CS060
  //   ZEROS
endmodule
