// Logisim project 23cs060_mco_exp_1 (2).circ as structural Verilog
module binary_to_7_bsegment_display (
  input  B3,
  input  B2,
  input  B1,
  input  B0,
  output A,
  output B,
  output C,
  output D,
  output E,
  output F,
  output G,
  output DP
);

  wire and_1_out, and_2_out, and_3_out, and_4_out, and_5_out, and_6_out, and_7_out, and_8_out, and_9_out,
       and_10_out, and_11_out, and_12_out, and_13_out, and_14_out, and_15_out, and_16_out, not_1_out,
       not_2_out, not_3_out, not_4_out, not_5_out, not_6_out, not_7_out, not_8_out, not_9_out, not_10_out,
       not_11_out, not_12_out, not_13_out, not_14_out, not_15_out, not_16_out, not_17_out, not_18_out,
       not_19_out, not_20_out, not_21_out;

  not not_1 (not_1_out, B2);
  and and_1 (and_1_out, not_1_out, not_2_out);
  not not_2 (not_2_out, B0);
  and and_2 (and_2_out, B2, B0);
  not not_3 (not_3_out, B2);
  not not_4 (not_4_out, B1);
  and and_3 (and_3_out, not_4_out, not_5_out);
  not not_5 (not_5_out, B0);
  and and_4 (and_4_out, B1, B0);
  not not_6 (not_6_out, B1);
  or or_1 (C, not_6_out, B0, B2);
  not not_7 (not_7_out, B2);
  and and_5 (and_5_out, not_7_out, not_8_out);
  not not_8 (not_8_out, B0);
  not not_9 (not_9_out, B2);
  and and_6 (and_6_out, not_9_out, B1);
  and and_7 (and_7_out, B1, not_10_out);
  not not_10 (not_10_out, B0);
  not not_11 (not_11_out, B1);
  and and_8 (and_8_out, B2, not_11_out, B0);
  not not_12 (not_12_out, B2);
  and and_9 (and_9_out, not_12_out, not_13_out);
  not not_13 (not_13_out, B0);
  and and_10 (and_10_out, B1, not_14_out);
  not not_14 (not_14_out, B0);
  not not_15 (not_15_out, B1);
  and and_11 (and_11_out, not_15_out, not_16_out);
  not not_16 (not_16_out, B0);
  and and_12 (and_12_out, B2, not_17_out);
  not not_17 (not_17_out, B1);
  and and_13 (and_13_out, B2, not_18_out);
  not not_18 (not_18_out, B0);
  not not_19 (not_19_out, B2);
  and and_14 (and_14_out, not_19_out, B1);
  and and_15 (and_15_out, B2, not_20_out);
  not not_20 (not_20_out, B1);
  and and_16 (and_16_out, B2, not_21_out);
  not not_21 (not_21_out, B0);
  or or_2 (A, and_1_out, B1, and_2_out, B3);
  or or_3 (B, not_3_out, and_3_out, and_4_out);
  or or_4 (D, and_5_out, and_6_out, and_7_out, and_8_out, B3);
  or or_5 (E, and_9_out, and_10_out);
  or or_6 (F, and_11_out, and_12_out, and_13_out, B3);
  or or_7 (G, and_14_out, and_15_out, and_16_out, B3);

  assign DP = 1'b0;

  // Notes on the sheet:
  //   23CS060
endmodule

module display_0_to_9 (
  input  [3:0] BCD_INPUT
);

  wire binary_to_7_bsegment_display_1_a, binary_to_7_bsegment_display_1_b, binary_to_7_bsegment_display_1_c,
       binary_to_7_bsegment_display_1_d, binary_to_7_bsegment_display_1_dp, binary_to_7_bsegment_display_1_e,
       binary_to_7_bsegment_display_1_f, binary_to_7_bsegment_display_1_g;

  binary_to_7_bsegment_display binary_to_7_bsegment_display_1 (
    .B3(BCD_INPUT[3]), .B2(BCD_INPUT[2]), .B1(BCD_INPUT[1]), .B0(BCD_INPUT[0]),
    .A(binary_to_7_bsegment_display_1_a), .B(binary_to_7_bsegment_display_1_b),
    .C(binary_to_7_bsegment_display_1_c), .D(binary_to_7_bsegment_display_1_d),
    .E(binary_to_7_bsegment_display_1_e), .F(binary_to_7_bsegment_display_1_f),
    .G(binary_to_7_bsegment_display_1_g), .DP(binary_to_7_bsegment_display_1_dp));
  _7_Segment_Display u_7_segment_display_1 (
    .g(binary_to_7_bsegment_display_1_g), .f(binary_to_7_bsegment_display_1_f),
    .a(binary_to_7_bsegment_display_1_a), .b(binary_to_7_bsegment_display_1_b),
    .e(binary_to_7_bsegment_display_1_e), .d(binary_to_7_bsegment_display_1_d),
    .c(binary_to_7_bsegment_display_1_c), .dp(binary_to_7_bsegment_display_1_dp));

  // Notes on the sheet:
  //   23CS060
endmodule

module binary_to_bcd (
  input  B6,
  input  B5,
  input  B4,
  input  B3,
  input  B2,
  input  B1,
  input  B0,
  output BCD1_3,
  output BCD1_2,
  output BCD1_1,
  output BCD1_0,
  output BCD0_3,
  output BCD0_2,
  output BCD0_1,
  output BCD0_0
);

  wire and_1_out, and_2_out, and_3_out, and_4_out, and_5_out, and_6_out, and_7_out, and_8_out, and_9_out,
       and_10_out, and_11_out, and_12_out, and_13_out, and_14_out, and_15_out, and_16_out, and_17_out,
       and_18_out, and_19_out, and_20_out, and_21_out, and_22_out, and_23_out, and_24_out, and_25_out,
       and_26_out, and_27_out, and_28_out, and_29_out, and_30_out, and_31_out, and_32_out, and_33_out,
       and_34_out, and_35_out, and_36_out, and_37_out, and_38_out, and_39_out, and_40_out, and_41_out,
       and_42_out, and_43_out, and_44_out, and_45_out, and_46_out, and_47_out, and_48_out, and_49_out,
       and_50_out, and_51_out, and_52_out, and_53_out, and_54_out, and_55_out, and_56_out, and_57_out,
       and_58_out, and_59_out, not_1_out, not_2_out, not_3_out, not_4_out, not_5_out, not_6_out, not_7_out,
       not_8_out, not_9_out, not_10_out, not_11_out, not_12_out, not_13_out, not_14_out, not_15_out,
       not_16_out, not_17_out, not_18_out, not_19_out, not_20_out, not_21_out, not_22_out, not_23_out,
       not_24_out, not_25_out, not_26_out, not_27_out, not_28_out, not_29_out, not_30_out, not_31_out,
       not_32_out, not_33_out, not_34_out, not_35_out, not_36_out, not_37_out, not_38_out, not_39_out,
       not_40_out, not_41_out, not_42_out, not_43_out, not_44_out, not_45_out, not_46_out, not_47_out,
       not_48_out, not_49_out, not_50_out, not_51_out, not_52_out, not_53_out, not_54_out, not_55_out,
       not_56_out, not_57_out, not_58_out, not_59_out, not_60_out, not_61_out, not_62_out, not_63_out,
       not_64_out, not_65_out, not_66_out, not_67_out, not_68_out, not_69_out, not_70_out, not_71_out,
       not_72_out, not_73_out, not_74_out, not_75_out, not_76_out, not_77_out, not_78_out, not_79_out,
       not_80_out, not_81_out, not_82_out, not_83_out, not_84_out, not_85_out, not_86_out, not_87_out,
       not_88_out, not_89_out, not_90_out, not_91_out, not_92_out, not_93_out, not_94_out, not_95_out,
       not_96_out, not_97_out, not_98_out, not_99_out, not_100_out, not_101_out, not_102_out, not_103_out,
       not_104_out, not_105_out, not_106_out, not_107_out, not_108_out, not_109_out, not_110_out,
       not_111_out, not_112_out, not_113_out, not_114_out, not_115_out;

  and and_1 (and_1_out, B1, B0);
  and and_2 (and_2_out, B2, B0);
  not not_1 (not_1_out, B2);
  not not_2 (not_2_out, B1);
  not not_3 (not_3_out, B2);
  not not_4 (not_4_out, B1);
  not not_5 (not_5_out, B3);
  not not_6 (not_6_out, B2);
  not not_7 (not_7_out, B0);
  not not_8 (not_8_out, B1);
  not not_9 (not_9_out, B0);
  not not_10 (not_10_out, B1);
  not not_11 (not_11_out, B0);
  not not_12 (not_12_out, B0);
  not not_13 (not_13_out, B3);
  not not_14 (not_14_out, B2);
  not not_15 (not_15_out, B4);
  not not_16 (not_16_out, B3);
  not not_17 (not_17_out, B1);
  not not_18 (not_18_out, B0);
  not not_19 (not_19_out, B2);
  not not_20 (not_20_out, B4);
  not not_21 (not_21_out, B3);
  not not_22 (not_22_out, B2);
  not not_23 (not_23_out, B1);
  not not_24 (not_24_out, B3);
  not not_25 (not_25_out, B2);
  not not_26 (not_26_out, B1);
  not not_27 (not_27_out, B2);
  not not_28 (not_28_out, B1);
  not not_29 (not_29_out, B5);
  not not_30 (not_30_out, B4);
  not not_31 (not_31_out, B3);
  not not_32 (not_32_out, B5);
  not not_33 (not_33_out, B4);
  not not_34 (not_34_out, B2);
  not not_35 (not_35_out, B1);
  not not_36 (not_36_out, B0);
  not not_37 (not_37_out, B5);
  not not_38 (not_38_out, B4);
  not not_39 (not_39_out, B5);
  not not_40 (not_40_out, B3);
  not not_41 (not_41_out, B2);
  not not_42 (not_42_out, B5);
  not not_43 (not_43_out, B1);
  not not_44 (not_44_out, B0);
  not not_45 (not_45_out, B4);
  not not_46 (not_46_out, B3);
  not not_47 (not_47_out, B1);
  not not_48 (not_48_out, B0);
  not not_49 (not_49_out, B4);
  not not_50 (not_50_out, B3);
  not not_51 (not_51_out, B2);
  not not_52 (not_52_out, B2);
  not not_53 (not_53_out, B5);
  not not_54 (not_54_out, B4);
  not not_55 (not_55_out, B3);
  not not_56 (not_56_out, B2);
  not not_57 (not_57_out, B5);
  not not_58 (not_58_out, B4);
  not not_59 (not_59_out, B1);
  not not_60 (not_60_out, B0);
  not not_61 (not_61_out, B5);
  not not_62 (not_62_out, B4);
  not not_63 (not_63_out, B0);
  not not_64 (not_64_out, B4);
  not not_65 (not_65_out, B1);
  not not_66 (not_66_out, B0);
  not not_67 (not_67_out, B3);
  not not_68 (not_68_out, B2);
  not not_69 (not_69_out, B1);
  not not_70 (not_70_out, B0);
  not not_71 (not_71_out, B5);
  not not_72 (not_72_out, B2);
  not not_73 (not_73_out, B3);
  not not_74 (not_74_out, B5);
  not not_75 (not_75_out, B2);
  not not_76 (not_76_out, B4);
  not not_77 (not_77_out, B2);
  not not_78 (not_78_out, B1);
  not not_79 (not_79_out, B4);
  not not_80 (not_80_out, B3);
  not not_81 (not_81_out, B2);
  not not_82 (not_82_out, B0);
  not not_83 (not_83_out, B3);
  not not_84 (not_84_out, B2);
  not not_85 (not_85_out, B0);
  not not_86 (not_86_out, B5);
  not not_87 (not_87_out, B3);
  not not_88 (not_88_out, B2);
  not not_89 (not_89_out, B5);
  not not_90 (not_90_out, B4);
  not not_91 (not_91_out, B3);
  not not_92 (not_92_out, B1);
  not not_93 (not_93_out, B0);
  not not_94 (not_94_out, B5);
  not not_95 (not_95_out, B2);
  not not_96 (not_96_out, B5);
  not not_97 (not_97_out, B4);
  not not_98 (not_98_out, B5);
  not not_99 (not_99_out, B3);
  not not_100 (not_100_out, B5);
  not not_101 (not_101_out, B2);
  not not_102 (not_102_out, B1);
  not not_103 (not_103_out, B5);
  not not_104 (not_104_out, B4);
  not not_105 (not_105_out, B3);
  not not_106 (not_106_out, B2);
  not not_107 (not_107_out, B1);
  not not_108 (not_108_out, B3);
  not not_109 (not_109_out, B2);
  not not_110 (not_110_out, B4);
  not not_111 (not_111_out, B1);
  not not_112 (not_112_out, B0);
  not not_113 (not_113_out, B3);
  not not_114 (not_114_out, B1);
  not not_115 (not_115_out, B0);
  or or_1 (BCD1_3, and_1_out, and_2_out);
  and and_3 (and_3_out, not_1_out, not_2_out, B0);
  and and_4 (and_4_out, B2, B1);
  and and_5 (and_5_out, B3, B1);
  and and_6 (and_6_out, not_3_out, not_4_out, B0);
  and and_7 (and_7_out, not_5_out, not_6_out, B1, not_7_out);
  and and_8 (and_8_out, B3, B2, not_8_out, not_9_out);
  and and_9 (and_9_out, B4, B2, not_10_out, not_11_out);
  and and_10 (and_10_out, B4, B3, B2, not_12_out);
  and and_11 (and_11_out, B6, B5, B4, B3, B2, B1);
  and and_12 (and_12_out, not_13_out, not_14_out, B1);
  and and_13 (and_13_out, not_15_out, not_16_out, B2, not_17_out, not_18_out);
  and and_14 (and_14_out, B3, not_19_out, B0);
  and and_15 (and_15_out, not_20_out, B3, B2, B1);
  and and_16 (and_16_out, B4, not_21_out, B1);
  and and_17 (and_17_out, B4, B3, not_22_out, not_23_out);
  and and_18 (and_18_out, B4, B3, B0);
  and and_19 (and_19_out, B5, not_24_out, B1);
  and and_20 (and_20_out, B5, B3, not_25_out, not_26_out);
  and and_21 (and_21_out, B5, B3, B0);
  and and_22 (and_22_out, B5, B4, not_27_out, B0);
  and and_23 (and_23_out, B5, B4, B3, not_28_out);
  and and_24 (and_24_out, not_29_out, not_30_out, not_31_out, B2, B1);
  and and_25 (and_25_out, not_32_out, not_33_out, B3, not_34_out, not_35_out, not_36_out);
  and and_26 (and_26_out, not_37_out, not_38_out, B3, B2, B0);
  and and_27 (and_27_out, not_39_out, B4, not_40_out, not_41_out, B0);
  and and_28 (and_28_out, not_42_out, B4, B3, B2, not_43_out, not_44_out);
  and and_29 (and_29_out, B5, B1, B0);
  and and_30 (and_30_out, B5, not_45_out, not_46_out, B2, not_47_out, not_48_out);
  and and_31 (and_31_out, B5, not_49_out, B3, B2, B1);
  and and_32 (and_32_out, B5, B4, not_50_out, not_51_out, B1);
  and and_33 (and_33_out, B5, B4, B3, not_52_out, B0);
  and and_34 (and_34_out, not_53_out, not_54_out, not_55_out, not_56_out, B0);
  and and_35 (and_35_out, not_57_out, not_58_out, B2, not_59_out, not_60_out);
  and and_36 (and_36_out, not_61_out, not_62_out, B3, B2, not_63_out);
  and and_37 (and_37_out, not_64_out, B3, B2, not_65_out, not_66_out);
  and and_38 (and_38_out, B4, not_67_out, not_68_out, not_69_out, not_70_out);
  and and_39 (and_39_out, not_71_out, B4, not_72_out, B1);
  and and_40 (and_40_out, B4, not_73_out, B2, B0);
  and and_41 (and_41_out, not_74_out, B4, B3, not_75_out, B0);
  and and_42 (and_42_out, B5, not_76_out, not_77_out, not_78_out, B0);
  and and_43 (and_43_out, B5, not_79_out, not_80_out, not_81_out, B1, not_82_out);
  and and_44 (and_44_out, B5, B4, B2, B0);
  and and_45 (and_45_out, B5, B4, not_83_out, B2, B1);
  and and_46 (and_46_out, B5, B4, B3, not_84_out, not_85_out);
  and and_47 (and_47_out, not_86_out, not_87_out, not_88_out, B1);
  and and_48 (and_48_out, not_89_out, not_90_out, not_91_out, B2, not_92_out, not_93_out);
  and and_49 (and_49_out, not_94_out, B3, not_95_out, B0);
  and and_50 (and_50_out, not_96_out, not_97_out, B3, B2, B1);
  and and_51 (and_51_out, not_98_out, B4, not_99_out, B1);
  and and_52 (and_52_out, not_100_out, B4, B3, not_101_out, not_102_out);
  and and_53 (and_53_out, not_103_out, B4, B3, B0);
  and and_54 (and_54_out, B5, not_104_out, not_105_out, not_106_out, not_107_out);
  and and_55 (and_55_out, B5, not_108_out, B2, B0);
  and and_56 (and_56_out, B5, B3, not_109_out, B1);
  and and_57 (and_57_out, B5, not_110_out, B3, B2, not_111_out, not_112_out);
  and and_58 (and_58_out, B5, B4, not_113_out, not_114_out, not_115_out);
  and and_59 (and_59_out, B5, B4, B3, B1);
  or or_2 (BCD1_2, and_3_out, and_4_out, and_5_out);
  or or_3 (BCD1_1, and_6_out, and_7_out, and_8_out, and_9_out, and_10_out, and_11_out);
  or or_4 (BCD1_0, and_12_out, and_13_out, and_14_out, and_15_out, and_16_out, and_17_out, and_18_out, and_19_out, and_20_out, and_21_out, and_22_out, and_23_out);
  or or_5 (BCD0_3, and_24_out, and_25_out, and_26_out, and_27_out, and_28_out, and_29_out, and_30_out, and_31_out, and_32_out, and_33_out);
  or or_6 (BCD0_2, and_34_out, and_35_out, and_36_out, and_37_out, and_38_out, and_39_out, and_40_out, and_41_out, and_42_out, and_43_out, and_44_out, and_45_out, and_46_out);
  or or_7 (BCD0_1, and_47_out, and_48_out, and_49_out, and_50_out, and_51_out, and_52_out, and_53_out, and_54_out, and_55_out, and_56_out, and_57_out, and_58_out, and_59_out);

  assign BCD0_0 = B6;
endmodule

module DISPLAY_0_TO_99 (
  input  [6:0] BINARY_INPUT
);

  wire binary_to_7_bsegment_display_1_a, binary_to_7_bsegment_display_1_b, binary_to_7_bsegment_display_1_c,
       binary_to_7_bsegment_display_1_d, binary_to_7_bsegment_display_1_dp, binary_to_7_bsegment_display_1_e,
       binary_to_7_bsegment_display_1_f, binary_to_7_bsegment_display_1_g, binary_to_7_bsegment_display_2_a,
       binary_to_7_bsegment_display_2_b, binary_to_7_bsegment_display_2_c, binary_to_7_bsegment_display_2_d,
       binary_to_7_bsegment_display_2_dp, binary_to_7_bsegment_display_2_e, binary_to_7_bsegment_display_2_f,
       binary_to_7_bsegment_display_2_g, binary_to_bcd_1_bcd0_0, binary_to_bcd_1_bcd0_1,
       binary_to_bcd_1_bcd0_2, binary_to_bcd_1_bcd0_3, binary_to_bcd_1_bcd1_0, binary_to_bcd_1_bcd1_1,
       binary_to_bcd_1_bcd1_2, binary_to_bcd_1_bcd1_3;

  binary_to_bcd binary_to_bcd_1 (
    .B6(BINARY_INPUT[0]), .B5(BINARY_INPUT[1]), .B4(BINARY_INPUT[2]), .B3(BINARY_INPUT[3]),
    .B2(BINARY_INPUT[4]), .B1(BINARY_INPUT[5]), .B0(BINARY_INPUT[6]), .BCD1_3(binary_to_bcd_1_bcd1_3),
    .BCD1_2(binary_to_bcd_1_bcd1_2), .BCD1_1(binary_to_bcd_1_bcd1_1), .BCD1_0(binary_to_bcd_1_bcd1_0),
    .BCD0_3(binary_to_bcd_1_bcd0_3), .BCD0_2(binary_to_bcd_1_bcd0_2), .BCD0_1(binary_to_bcd_1_bcd0_1),
    .BCD0_0(binary_to_bcd_1_bcd0_0));
  binary_to_7_bsegment_display binary_to_7_bsegment_display_1 (
    .B3(binary_to_bcd_1_bcd1_3), .B2(binary_to_bcd_1_bcd1_2), .B1(binary_to_bcd_1_bcd1_1),
    .B0(binary_to_bcd_1_bcd1_0), .A(binary_to_7_bsegment_display_1_a), .B(binary_to_7_bsegment_display_1_b),
    .C(binary_to_7_bsegment_display_1_c), .D(binary_to_7_bsegment_display_1_d),
    .E(binary_to_7_bsegment_display_1_e), .F(binary_to_7_bsegment_display_1_f),
    .G(binary_to_7_bsegment_display_1_g), .DP(binary_to_7_bsegment_display_1_dp));
  binary_to_7_bsegment_display binary_to_7_bsegment_display_2 (
    .B3(binary_to_bcd_1_bcd0_3), .B2(binary_to_bcd_1_bcd0_2), .B1(binary_to_bcd_1_bcd0_1),
    .B0(binary_to_bcd_1_bcd0_0), .A(binary_to_7_bsegment_display_2_a), .B(binary_to_7_bsegment_display_2_b),
    .C(binary_to_7_bsegment_display_2_c), .D(binary_to_7_bsegment_display_2_d),
    .E(binary_to_7_bsegment_display_2_e), .F(binary_to_7_bsegment_display_2_f),
    .G(binary_to_7_bsegment_display_2_g), .DP(binary_to_7_bsegment_display_2_dp));
  _7_Segment_Display u_7_segment_display_1 (
    .g(binary_to_7_bsegment_display_1_g), .f(binary_to_7_bsegment_display_1_f),
    .a(binary_to_7_bsegment_display_1_a), .b(binary_to_7_bsegment_display_1_b),
    .e(binary_to_7_bsegment_display_1_e), .d(binary_to_7_bsegment_display_1_d),
    .c(binary_to_7_bsegment_display_1_c), .dp(binary_to_7_bsegment_display_1_dp));
  _7_Segment_Display u_7_segment_display_2 (
    .g(binary_to_7_bsegment_display_2_g), .f(binary_to_7_bsegment_display_2_f),
    .a(binary_to_7_bsegment_display_2_a), .b(binary_to_7_bsegment_display_2_b),
    .e(binary_to_7_bsegment_display_2_e), .d(binary_to_7_bsegment_display_2_d),
    .c(binary_to_7_bsegment_display_2_c), .dp(binary_to_7_bsegment_display_2_dp));

  // Notes on the sheet:
  //   23CS060
endmodule
