// Logisim project 23cs060_mco_exp_1.circ as structural Verilog
module main (
  input  B6,
  input  B5,
  input  B4,
  input  B3,
  input  B2,
  input  B1,
  input  B0,
  output BCD1_3,
  output BCD1_2,
  output BCD1_1,
  output BCD1_0,
  output BCD0_3,
  output BCD0_2,
  output BCD0_1,
  output BCD0_0
);

  wire and_1_out, and_2_out, and_3_out, and_4_out, and_5_out, and_6_out, and_7_out, and_8_out, and_9_out,
       and_10_out, and_11_out, and_12_out, and_13_out, and_14_out, and_15_out, and_16_out, and_17_out,
       and_18_out, and_19_out, and_20_out, and_21_out, and_22_out, and_23_out, and_24_out, and_25_out,
       and_26_out, and_27_out, and_28_out, and_29_out, and_30_out, and_31_out, and_32_out, and_33_out,
       and_34_out, and_35_out, and_36_out, not_1_out, not_2_out, not_3_out, not_4_out, not_5_out, not_6_out,
       not_7_out, not_8_out, not_9_out, not_10_out, not_11_out, not_12_out, not_13_out, not_14_out,
       not_15_out, not_16_out, not_17_out, not_18_out, not_19_out, not_20_out, not_21_out, not_22_out,
       not_23_out, not_24_out, not_25_out, not_26_out, not_27_out, not_28_out, not_29_out, not_30_out,
       not_31_out, not_32_out, not_33_out, not_34_out, not_35_out, not_36_out, not_37_out, not_38_out,
       not_39_out, not_40_out, not_41_out, not_42_out, not_43_out, not_44_out, not_45_out, not_46_out,
       not_47_out, not_48_out, not_49_out, not_50_out, not_51_out, not_52_out, not_53_out, not_54_out,
       not_55_out, not_56_out, not_57_out, not_58_out, not_59_out, not_60_out, not_61_out, not_62_out,
       not_63_out, not_64_out, not_65_out, not_66_out, not_67_out, not_68_out, not_69_out, not_70_out,
       not_71_out, not_72_out, not_73_out, not_74_out, not_75_out, not_76_out, not_77_out, not_78_out,
       not_79_out, not_80_out, not_81_out, not_82_out, not_83_out, not_84_out, not_85_out, not_86_out,
       not_87_out;

  not not_1 (not_1_out, B6);
  not not_2 (not_2_out, B5);
  not not_3 (not_3_out, B4);
  not not_4 (not_4_out, B2);
  not not_5 (not_5_out, B1);
  not not_6 (not_6_out, B6);
  not not_7 (not_7_out, B5);
  not not_8 (not_8_out, B3);
  not not_9 (not_9_out, B2);
  not not_10 (not_10_out, B6);
  not not_11 (not_11_out, B5);
  not not_12 (not_12_out, B1);
  not not_13 (not_13_out, B4);
  not not_14 (not_14_out, B3);
  not not_15 (not_15_out, B3);
  not not_16 (not_16_out, B2);
  not not_17 (not_17_out, B1);
  not not_18 (not_18_out, B2);
  not not_19 (not_19_out, B4);
  not not_20 (not_20_out, B3);
  not not_21 (not_21_out, B1);
  not not_22 (not_22_out, B4);
  not not_23 (not_23_out, B2);
  not not_24 (not_24_out, B1);
  not not_25 (not_25_out, B6);
  not not_26 (not_26_out, B5);
  not not_27 (not_27_out, B4);
  not not_28 (not_28_out, B3);
  not not_29 (not_29_out, B6);
  not not_30 (not_30_out, B4);
  not not_31 (not_31_out, B6);
  not not_32 (not_32_out, B5);
  not not_33 (not_33_out, B2);
  not not_34 (not_34_out, B1);
  not not_35 (not_35_out, B6);
  not not_36 (not_36_out, B5);
  not not_37 (not_37_out, B2);
  not not_38 (not_38_out, B6);
  not not_39 (not_39_out, B2);
  not not_40 (not_40_out, B1);
  not not_41 (not_41_out, B6);
  not not_42 (not_42_out, B4);
  not not_43 (not_43_out, B3);
  not not_44 (not_44_out, B2);
  not not_45 (not_45_out, B4);
  not not_46 (not_46_out, B1);
  not not_47 (not_47_out, B3);
  not not_48 (not_48_out, B4);
  not not_49 (not_49_out, B3);
  not not_50 (not_50_out, B2);
  not not_51 (not_51_out, B1);
  not not_52 (not_52_out, B5);
  not not_53 (not_53_out, B4);
  not not_54 (not_54_out, B2);
  not not_55 (not_55_out, B4);
  not not_56 (not_56_out, B1);
  not not_57 (not_57_out, B3);
  not not_58 (not_58_out, B5);
  not not_59 (not_59_out, B4);
  not not_60 (not_60_out, B3);
  not not_61 (not_61_out, B2);
  not not_62 (not_62_out, B6);
  not not_63 (not_63_out, B5);
  not not_64 (not_64_out, B3);
  not not_65 (not_65_out, B5);
  not not_66 (not_66_out, B4);
  not not_67 (not_67_out, B1);
  not not_68 (not_68_out, B6);
  not not_69 (not_69_out, B5);
  not not_70 (not_70_out, B3);
  not not_71 (not_71_out, B2);
  not not_72 (not_72_out, B1);
  not not_73 (not_73_out, B6);
  not not_74 (not_74_out, B5);
  not not_75 (not_75_out, B2);
  not not_76 (not_76_out, B4);
  not not_77 (not_77_out, B3);
  not not_78 (not_78_out, B1);
  not not_79 (not_79_out, B3);
  not not_80 (not_80_out, B1);
  not not_81 (not_81_out, B4);
  not not_82 (not_82_out, B2);
  not not_83 (not_83_out, B1);
  not not_84 (not_84_out, B4);
  not not_85 (not_85_out, B1);
  not not_86 (not_86_out, B1);
  not not_87 (not_87_out, B3);
  and and_1 (and_1_out, not_1_out, not_2_out, not_3_out, B3, not_4_out, not_5_out);
  and and_2 (and_2_out, not_6_out, not_7_out, B4, not_8_out, not_9_out, B1);
  and and_3 (and_3_out, not_10_out, not_11_out, B4, B3, B2, not_12_out);
  and and_4 (and_4_out, B5, not_13_out, not_14_out, B2, B1);
  and and_5 (and_5_out, B5, B4, not_15_out, not_16_out, not_17_out);
  and and_6 (and_6_out, B5, B4, B3, not_18_out, B1);
  and and_7 (and_7_out, B6, not_19_out, not_20_out, B2, not_21_out);
  and and_8 (and_8_out, B6, not_22_out, B3, B2, B1);
  and and_9 (and_9_out, B6, B4, B3, not_23_out, not_24_out);
  and and_10 (and_10_out, B6, B5, B1);
  and and_11 (and_11_out, not_25_out, not_26_out, not_27_out, not_28_out, B2);
  and and_12 (and_12_out, not_29_out, not_30_out, B3, B2, B1);
  and and_13 (and_13_out, not_31_out, not_32_out, B4, not_33_out, not_34_out);
  and and_14 (and_14_out, not_35_out, not_36_out, B4, B3, not_37_out);
  and and_15 (and_15_out, not_38_out, B4, B3, not_39_out, not_40_out);
  and and_16 (and_16_out, not_41_out, B5, not_42_out, not_43_out, not_44_out, B1);
  and and_17 (and_17_out, B5, not_45_out, B2, not_46_out);
  and and_18 (and_18_out, B5, B4, not_47_out, B2, B1);
  and and_19 (and_19_out, B6, not_48_out, not_49_out, not_50_out, not_51_out);
  and and_20 (and_20_out, B6, not_52_out, not_53_out, not_54_out, B1);
  and and_21 (and_21_out, B6, not_55_out, B3, B2, not_56_out);
  and and_22 (and_22_out, B6, B4, not_57_out, B2);
  and and_23 (and_23_out, B6, B4, B2, B1);
  and and_24 (and_24_out, not_58_out, not_59_out, not_60_out, not_61_out, B1);
  and and_25 (and_25_out, not_62_out, not_63_out, not_64_out, B2, B1);
  and and_26 (and_26_out, not_65_out, not_66_out, B3, B2, not_67_out);
  and and_27 (and_27_out, not_68_out, not_69_out, B4, not_70_out, not_71_out, not_72_out);
  and and_28 (and_28_out, not_73_out, not_74_out, B4, B3, not_75_out, B1);
  and and_29 (and_29_out, B5, not_76_out, not_77_out, not_78_out);
  and and_30 (and_30_out, B5, not_79_out, B2, not_80_out);
  and and_31 (and_31_out, B5, not_81_out, B3, B1);
  and and_32 (and_32_out, B5, B3, B2, B1);
  and and_33 (and_33_out, B5, B4, B3, not_82_out, not_83_out);
  and and_34 (and_34_out, B6, not_84_out, B3, not_85_out);
  and and_35 (and_35_out, B6, B3, B2, not_86_out);
  and and_36 (and_36_out, B6, B4, not_87_out, B1);
  or or_1 (BCD0_3, and_1_out, and_2_out, and_3_out, and_4_out, and_5_out, and_6_out, and_7_out, and_8_out, and_9_out, and_10_out);
  or or_2 (BCD0_2, and_11_out, and_12_out, and_13_out, and_14_out, and_15_out, and_16_out, and_17_out, and_18_out, and_19_out, and_20_out, and_21_out, and_22_out, and_23_out);
  or or_3 (BCD0_1, and_24_out, and_25_out, and_26_out, and_27_out, and_28_out, and_29_out, and_30_out, and_31_out, and_32_out, and_33_out, and_34_out, and_35_out, and_36_out);

  assign BCD0_0 = B0;
  assign BCD1_0 = 1'b0;
  assign BCD1_1 = 1'b0;
  assign BCD1_2 = 1'b0;
  assign BCD1_3 = 1'b0;
endmodule

module binary_7_segment_led (
  input  b3,
  input  b2,
  input  b1,
  input  b0,
  output a,
  output b,
  output c,
  output d,
  output e,
  output f,
  output g,
  output dp
);

  wire and_1_out, and_2_out, and_3_out, and_4_out, and_5_out, and_6_out, and_7_out, and_8_out, and_9_out,
       and_10_out, and_11_out, and_12_out, and_13_out, and_14_out, and_15_out, and_16_out, and_17_out,
       and_18_out, and_19_out, not_1_out, not_2_out, not_3_out, not_4_out, not_5_out, not_6_out, not_7_out,
       not_8_out, not_9_out, not_10_out, not_11_out, not_12_out, not_13_out, not_14_out, not_15_out,
       not_16_out, not_17_out, not_18_out, not_19_out, not_20_out, not_21_out, not_22_out, not_23_out,
       not_24_out, not_25_out;

  not not_1 (not_1_out, b2);
  and and_1 (and_1_out, not_1_out, not_2_out);
  not not_2 (not_2_out, b0);
  and and_2 (and_2_out, b2, b0);
  not not_3 (not_3_out, b3);
  and and_3 (and_3_out, not_3_out, not_4_out);
  not not_4 (not_4_out, b2);
  not not_5 (not_5_out, b2);
  and and_4 (and_4_out, not_5_out, not_6_out);
  not not_6 (not_6_out, b1);
  not not_7 (not_7_out, b1);
  and and_5 (and_5_out, not_7_out, not_8_out);
  not not_8 (not_8_out, b0);
  and and_6 (and_6_out, b1, b0);
  not not_9 (not_9_out, b1);
  or or_1 (c, not_9_out, b0, b2);
  not not_10 (not_10_out, b2);
  and and_7 (and_7_out, not_10_out, not_11_out);
  not not_11 (not_11_out, b0);
  not not_12 (not_12_out, b2);
  and and_8 (and_8_out, not_12_out, b1);
  and and_9 (and_9_out, b1, not_13_out);
  not not_13 (not_13_out, b0);
  not not_14 (not_14_out, b1);
  and and_10 (and_10_out, b2, not_14_out, b0);
  not not_15 (not_15_out, b2);
  and and_11 (and_11_out, not_15_out, not_16_out);
  not not_16 (not_16_out, b0);
  and and_12 (and_12_out, b1, not_17_out);
  not not_17 (not_17_out, b0);
  not not_18 (not_18_out, b1);
  and and_13 (and_13_out, not_18_out, not_19_out);
  not not_19 (not_19_out, b0);
  and and_14 (and_14_out, b2, not_20_out);
  not not_20 (not_20_out, b1);
  and and_15 (and_15_out, b2, not_21_out);
  not not_21 (not_21_out, b0);
  not not_22 (not_22_out, b2);
  and and_16 (and_16_out, not_22_out, b1);
  and and_17 (and_17_out, b2, not_23_out);
  not not_23 (not_23_out, b1);
  and and_18 (and_18_out, b2, not_24_out);
  not not_24 (not_24_out, b0);
  and and_19 (and_19_out, b3, not_25_out);
  not not_25 (not_25_out, b2);
  or or_2 (a, and_1_out, b1, and_2_out, b3);
  or or_3 (b, and_3_out, and_4_out, and_5_out, and_6_out);
  or or_4 (d, and_7_out, and_8_out, and_9_out, and_10_out, b3);
  or or_5 (e, and_11_out, and_12_out);
  or or_6 (f, and_13_out, and_14_out, and_15_out, b3);
  or or_7 (g, and_16_out, and_17_out, and_18_out, and_19_out);

  assign dp = 1'b0;
endmodule

module display_0_to9 (
  input  [3:0] in_1
);

  wire binary_7_segment_led_1_a, binary_7_segment_led_1_b, binary_7_segment_led_1_c,
       binary_7_segment_led_1_d, binary_7_segment_led_1_dp, binary_7_segment_led_1_e,
       binary_7_segment_led_1_f, binary_7_segment_led_1_g;

  binary_7_segment_led binary_7_segment_led_1 (
    .b3(in_1[3]), .b2(in_1[2]), .b1(in_1[1]), .b0(in_1[0]), .a(binary_7_segment_led_1_a),
    .b(binary_7_segment_led_1_b), .c(binary_7_segment_led_1_c), .d(binary_7_segment_led_1_d),
    .e(binary_7_segment_led_1_e), .f(binary_7_segment_led_1_f), .g(binary_7_segment_led_1_g),
    .dp(binary_7_segment_led_1_dp));
  _7_Segment_Display u_7_segment_display_1 (
    .g(binary_7_segment_led_1_g), .f(binary_7_segment_led_1_f), .a(binary_7_segment_led_1_a),
    .b(binary_7_segment_led_1_b), .e(binary_7_segment_led_1_e), .d(binary_7_segment_led_1_d),
    .c(binary_7_segment_led_1_c), .dp(binary_7_segment_led_1_dp));
endmodule

module _0_TO_99 (
  input  [6:0] in_1
);

  binary_7_segment_led binary_7_segment_led_1 ();  // open: b3, b2, b1, b0, a, b, c, d, e, f, g, dp
  main main_1 ();  // open: B6, B5, B4, B3, B2, B1, B0, BCD1_3, BCD1_2, BCD1_1, BCD1_0, BCD0_3, BCD0_2, BCD0_1, BCD0_0
  _7_Segment_Display u_7_segment_display_1 ();  // open: g, f, a, b, e, d, c, dp
  binary_7_segment_led binary_7_segment_led_2 ();  // open: b3, b2, b1, b0, a, b, c, d, e, f, g, dp
  _7_Segment_Display u_7_segment_display_2 ();  // open: g, f, a, b, e, d, c, dp
endmodule
