// Logisim project exp-2_MCO_23cs060.circ as structural Verilog: 1 circuit, main circuit main
module main (
  input  As,
  input  Bs,
  input  MOD_CONROL,
  input  [6:0] A,
  input  [6:0] B,
  output out_6,
  output CALL,
  output [6:0] RESULT_A,
  output E,
  output [6:0] FINAL_A,
  output FIANL_As,
  output AVF
);

  wire comparator_1_eq, multiplexer_2_out, multiplexer_4_out, not_3_out;
  wire [6:0] adder_2_out, multiplexer_1_out, multiplexer_3_out, not_1_out, not_2_out;

  xor xor_1 (out_6, As, Bs);
  assign not_1_out = ~B;  // NOT_Gate not_1, 7 bits wide
  Multiplexer #(.width(7), .enable("false")) multiplexer_1 (
    .in0(B), .in1(not_1_out), .out(multiplexer_1_out), .sel(CALL));
  Comparator #(.width(7)) comparator_1 (.a(RESULT_A), .b({7{1'b0}}), .eq(comparator_1_eq));  // open: gt, lt
  xor xor_2 (CALL, out_6, MOD_CONROL);
  Adder #(.width(7)) adder_1 (.a(A), .b(multiplexer_1_out), .out(RESULT_A), .cin(CALL), .cout(E));
  Multiplexer #(.enable("false")) multiplexer_2 (.in0(As), .in1(1'b0), .out(multiplexer_2_out), .sel(comparator_1_eq));
  assign not_2_out = ~RESULT_A;  // NOT_Gate not_2, 7 bits wide
  not not_3 (not_3_out, As);
  Adder #(.width(7)) adder_2 (.a(not_2_out), .b({7{1'b0}}), .out(adder_2_out), .cin(CALL));  // open: cout
  Multiplexer #(.width(7), .enable("false")) multiplexer_3 (
    .in0(adder_2_out), .in1(RESULT_A), .out(multiplexer_3_out), .sel(E));
  Multiplexer #(.enable("false")) multiplexer_4 (
    .in0(not_3_out), .in1(multiplexer_2_out), .out(multiplexer_4_out), .sel(E));
  Multiplexer #(.width(7), .enable("false")) multiplexer_5 (
    .in0(RESULT_A), .in1(multiplexer_3_out), .out(FINAL_A), .sel(CALL));
  Multiplexer #(.enable("false")) multiplexer_6 (.in0(As), .in1(multiplexer_4_out), .out(FIANL_As), .sel(CALL));
  Multiplexer #(.enable("false")) multiplexer_7 (.in0(E), .in1(1'b0), .out(AVF), .sel(CALL));

  // Notes on the sheet:
  //   sign bit of A
  //   sign bit of B
  //   MAGNITUDE PART OF A
  //   MAGNITUDE PART OF B
  //   sign=0 both have same sign
  //   sign=1 both have diff same sign
  //   MOD=0 :ADDITION
  //   MOD=1 :SUBTRACTION
  //   23CS060
  //   CALL=0:FUNCTION 1
  //   CALL=1:FUNCTION 2
  //   FUNCTION:1 ADD TWO NUMBERS AND SIGN OF NUMBER A
  //   FUNCTION:2 SUBTRACT SMALLER NUMBER WITH LARGER AND THE SIGGN OF LARGER NUMBER
endmodule
